# Fritzing sketch jcscpu-hmc_flag_lines (saved by Fritzing 0.9.4)
breadboards: 14

parts:
  Part1 = Arduino Nano (Rev3.0) (ICSP)  # not connected
  Part2 = Arduino Nano (Rev3.0) (ICSP)  # not connected
  Part3 = Arduino Nano (Rev3.0) (ICSP)  # not connected
  Part4 = Arduino Nano (Rev3.0) (ICSP)  # not connected
  SN74HC374 = IC, DIP package, 20 pins [chip_label=SN74HC373]
  SN74HC04 = IC, DIP package, 14 pins [chip_label=SN74HC08]
  SN74HC32 = IC, DIP package, 14 pins [chip_label=SN74HC32]
  R41 = Resistor [tolerance=±5% resistance=1k package=THT]
  R42 = Resistor [tolerance=±5% resistance=1k package=THT]
  R80 = Resistor [tolerance=±5% resistance=1k package=THT]
  R81 = Resistor [tolerance=±5% resistance=1k package=THT]
  LED93 = LED - 3mm [color="Blue (505nm)" package="3 mm [THT]"]
  LED94 = LED - 3mm [color="Blue (505nm)" package="3 mm [THT]"]
  LED95 = LED - 3mm [color="Blue (505nm)" package="3 mm [THT]"]
  LED96 = LED - 3mm [color="Blue (505nm)" package="3 mm [THT]"]

nets:
  N1: SN74HC374.pin1, SN74HC374.pin10, R41.Pin_0, R42.Pin_0, R80.Pin_0, R81.Pin_0
  N2: SN74HC374.pin2, SN74HC04.pin12, LED95.anode
  N3: SN74HC374.pin5, SN74HC04.pin9, LED93.anode
  N4: SN74HC374.pin6, SN74HC04.pin2, LED94.anode
  N5: SN74HC374.pin9, SN74HC04.pin5, LED96.anode
  N6: SN74HC04.pin3, SN74HC32.pin4
  N7: SN74HC04.pin6, SN74HC32.pin5
  N8: SN74HC04.pin7, SN74HC32.pin7
  N9: SN74HC04.pin8, SN74HC32.pin11
  N10: SN74HC04.pin11, SN74HC32.pin9
  N11: SN74HC04.pin14, SN74HC32.pin14
  N12: R41.Pin_1, LED93.cathode
  N13: R42.Pin_1, LED96.cathode
  N14: R80.Pin_1, LED94.cathode
  N15: R81.Pin_1, LED95.cathode

notes:
  R1_s
