# Fritzing sketch jcscpu-hmc (saved by Fritzing 0.9.4)
breadboards: 16

parts:
  Part1 = Arduino Nano (Rev3.0) (ICSP)
  Part2 = Arduino Nano (Rev3.0) (ICSP)
  Part3 = Arduino Nano (Rev3.0) (ICSP)
  Part4 = Arduino Nano (Rev3.0) (ICSP)
  Part5 = Arduino Nano (Rev3.0) (ICSP)
  SW1 = DIP Switch 8 Position [package=dipswitch-08]
  LED41 = smd LED [color="Green (555nm)" package="1206 [SMD]"]
  S1 = Pushbutton [package="[SMD]"]
  U28 = 74HC595 [package="DIP16 [THT]"]  # not connected
  U29 = 74HC595 [package="DIP16 [THT]"]
  U30 = 74HC595 [package="DIP16 [THT]"]  # not connected
  U31 = 74HC595 [package="DIP16 [THT]"]  # not connected
  R32 = Resistor [tolerance=±5% resistance=10k package="0402 [SMD]"]
  R33 = Resistor [tolerance=±5% resistance=10k package="0402 [SMD]"]
  R34 = Resistor [tolerance=±5% resistance=10k package="0402 [SMD]"]
  R35 = Resistor [tolerance=±5% resistance=10k package="0402 [SMD]"]
  R36 = Resistor [tolerance=±5% resistance=10k package="0402 [SMD]"]
  R37 = Resistor [tolerance=±5% resistance=10k package="0402 [SMD]"]
  R38 = Resistor [tolerance=±5% resistance=10k package="0402 [SMD]"]
  R5 = Resistor [tolerance=±5% resistance=1k package=THT]
  R7 = Resistor [tolerance=±5% resistance=1k package=THT]
  R6 = Resistor [tolerance=±5% resistance=1k package=THT]
  R4 = Resistor [tolerance=±5% resistance=1k package=THT]
  R3 = Resistor [tolerance=±5% resistance=1k package=THT]
  R2 = Resistor [tolerance=±5% resistance=1k package=THT]
  R8 = Resistor [tolerance=±5% resistance=1k package=THT]
  R1 = Resistor [tolerance=±5% resistance=1k package=THT]
  LED53 = smd LED [color="Green (555nm)" package="1206 [SMD]"]
  LED54 = smd LED [color="Green (555nm)" package="1206 [SMD]"]
  LED55 = smd LED [color="Green (555nm)" package="1206 [SMD]"]
  LED56 = smd LED [color="Green (555nm)" package="1206 [SMD]"]
  LED57 = smd LED [color="Green (555nm)" package="1206 [SMD]"]
  LED58 = smd LED [color="Green (555nm)" package="1206 [SMD]"]
  LED59 = smd LED [color="Green (555nm)" package="1206 [SMD]"]
  R39 = Resistor [tolerance=±5% resistance=10k package="0402 [SMD]"]
  SN74HC373 = IC, DIP package, 20 pins [chip_label=SN74HC373]
  SN74HC376 = IC, DIP package, 20 pins [chip_label=SN74HC373]
  SN74HC377 = IC, DIP package, 20 pins [chip_label=SN74HC373]
  SN74HC378 = IC, DIP package, 20 pins [chip_label=SN74HC373]
  SN74HC379 = IC, DIP package, 20 pins [chip_label=SN74HC373]
  SN74HC374 = IC, DIP package, 20 pins [chip_label=SN74HC373]
  LED65 = smd LED [color="Blue (505nm)" package="1206 [SMD]"]
  LED66 = smd LED [color="Blue (505nm)" package="1206 [SMD]"]
  LED67 = smd LED [color="Blue (505nm)" package="1206 [SMD]"]
  LED68 = smd LED [color="Blue (505nm)" package="1206 [SMD]"]
  LED69 = smd LED [color="Green (555nm)" package="1206 [SMD]"]
  LED70 = smd LED [color="Blue (505nm)" package="1206 [SMD]"]
  LED71 = smd LED [color="Blue (505nm)" package="1206 [SMD]"]
  LED72 = smd LED [color="Blue (505nm)" package="1206 [SMD]"]
  LED73 = smd LED [color="Red (633nm)" package="1206 [SMD]"]
  LED74 = smd LED [color="Green (555nm)" package="1206 [SMD]"]
  LED76 = smd LED [color="Green (555nm)" package="1206 [SMD]"]
  LED77 = smd LED [color="Blue (505nm)" package="1206 [SMD]"]
  LED78 = smd LED [color="Blue (505nm)" package="1206 [SMD]"]
  LED79 = smd LED [color="Blue (505nm)" package="1206 [SMD]"]
  LED80 = smd LED [color="Blue (505nm)" package="1206 [SMD]"]
  LED81 = smd LED [color="Blue (505nm)" package="1206 [SMD]"]  # not connected
  LED82 = smd LED [color="Blue (505nm)" package="1206 [SMD]"]  # not connected
  LED83 = smd LED [color="Yellow (595nm)" package="1206 [SMD]"]
  LED84 = smd LED [color="Yellow (595nm)" package="1206 [SMD]"]
  SN74HC00 = IC, DIP package, 14 pins [chip_label=SN74HC00]
  SN74HC380 = IC, DIP package, 14 pins [chip_label=SN74HC00]
  SN74HC381 = IC, DIP package, 20 pins [chip_label=SN74HC373]
  LED85 = smd LED [color="Red (633nm)" package="1206 [SMD]"]
  LED86 = smd LED [color="Red (633nm)" package="1206 [SMD]"]
  LED87 = smd LED [color="Red (633nm)" package="1206 [SMD]"]
  LED88 = smd LED [color="Red (633nm)" package="1206 [SMD]"]
  LED89 = smd LED [color="Red (633nm)" package="1206 [SMD]"]
  LED90 = smd LED [color="Red (633nm)" package="1206 [SMD]"]
  LED91 = smd LED [color="Red (633nm)" package="1206 [SMD]"]
  R44 = Resistor [tolerance=±5% resistance=1k package=THT]
  R45 = Resistor [tolerance=±5% resistance=1k package=THT]
  R47 = Resistor [tolerance=±5% resistance=1k package=THT]
  R48 = Resistor [tolerance=±5% resistance=1k package=THT]
  R49 = Resistor [tolerance=±5% resistance=1k package=THT]
  R50 = Resistor [tolerance=±5% resistance=1k package=THT]
  R51 = Resistor [tolerance=±5% resistance=1k package=THT]
  LED92 = smd LED [color="Yellow (595nm)" package="1206 [SMD]"]  # not connected
  LED93 = smd LED [color="Yellow (595nm)" package="1206 [SMD]"]
  LED94 = smd LED [color="Yellow (595nm)" package="1206 [SMD]"]  # not connected
  LED95 = smd LED [color="Yellow (595nm)" package="1206 [SMD]"]  # not connected
  LED96 = smd LED [color="Yellow (595nm)" package="1206 [SMD]"]
  LED97 = smd LED [color="Yellow (595nm)" package="1206 [SMD]"]
  LED98 = smd LED [color="Yellow (595nm)" package="1206 [SMD]"]
  LED99 = smd LED [color="Red (633nm)" package="1206 [SMD]"]
  R52 = Resistor [tolerance=±5% resistance=1k package=THT]
  R53 = Resistor [tolerance=±5% resistance=10k package="0402 [SMD]"]
  LED100 = smd LED [color="Yellow (595nm)" package="1206 [SMD]"]  # not connected
  SN74HC382 = IC, DIP package, 14 pins [chip_label=SN74HC00]
  LED101 = smd LED [color="Yellow (595nm)" package="1206 [SMD]"]
  SN74HC383 = IC, DIP package, 14 pins [chip_label=SN74HC00]
  LED102 = smd LED [color="Yellow (595nm)" package="1206 [SMD]"]
  LED103 = smd LED [color="Yellow (595nm)" package="1206 [SMD]"]
  LED104 = smd LED [color="Yellow (595nm)" package="1206 [SMD]"]
  SN74HC04 = IC, DIP package, 14 pins [chip_label=SN74HC04]
  SN74HC32 = IC, DIP package, 14 pins [chip_label=SN74HC32]
  R54 = Resistor [tolerance=±5% resistance=1k package=THT]
  LED105 = smd LED [color="Yellow (595nm)" package="1206 [SMD]"]
  SN74HC384 = IC, DIP package, 14 pins [chip_label=SN74HC00]
  R43 = Resistor [tolerance=±5% resistance=1k package=THT]
  R40 = Resistor [tolerance=±5% resistance=1k package=THT]
  R41 = Resistor [tolerance=±5% resistance=1k package=THT]
  R42 = Resistor [tolerance=±5% resistance=1k package=THT]
  LED64 = smd LED [color="Red (633nm)" package="1206 [SMD]"]

nets:
  N1: Part1.D1/TX, Part5.D1/TX
  N2: Part1.D0/RX, Part5.D0/RX
  N3: Part1.RESET, Part5.RESET
  GND: Part1.GND, Part2.GND, Part5.GND, R5.Pin_0, R7.Pin_0, R6.Pin_0, R4.Pin_0, R3.Pin_0, R2.Pin_0, R8.Pin_0, R1.Pin_0, SN74HC374.pin10, SN74HC00.pin7, SN74HC380.pin7, SN74HC382.pin7, SN74HC383.pin7, SN74HC384.pin7
  N4: Part1.D2, Part5.D2, LED74.anode
  N5: Part1.D3, Part5.D3, LED76.anode
  N6: Part1.D4, Part5.D4, LED69.anode
  N7: Part1.D5, Part5.D5, SW1.9, LED41.anode, R38.Pin_0, SN74HC373.pin2, SN74HC373.pin3, SN74HC376.pin2, SN74HC376.pin3, SN74HC377.pin2, SN74HC377.pin3, SN74HC378.pin2, SN74HC378.pin3, SN74HC379.pin2, SN74HC379.pin3, SN74HC381.pin2, SN74HC381.pin3
  N8: Part1.D6, Part5.D6, SW1.10, R37.Pin_0, LED53.anode, SN74HC373.pin4, SN74HC373.pin5, SN74HC376.pin4, SN74HC376.pin5, SN74HC377.pin4, SN74HC377.pin5, SN74HC378.pin4, SN74HC378.pin5, SN74HC379.pin4, SN74HC379.pin5, SN74HC381.pin4, SN74HC381.pin5
  N9: Part1.D7, Part5.D7, SW1.11, LED54.anode, R39.Pin_0, SN74HC373.pin6, SN74HC373.pin7, SN74HC376.pin6, SN74HC376.pin7, SN74HC377.pin7, SN74HC378.pin6, SN74HC378.pin7, SN74HC379.pin7, SN74HC381.pin6, SN74HC381.pin7
  N10: Part1.D8, Part5.D8, SW1.12, R36.Pin_0, LED55.anode, SN74HC373.pin8, SN74HC373.pin9, SN74HC376.pin8, SN74HC376.pin9, SN74HC377.pin8, SN74HC377.pin9, SN74HC378.pin8, SN74HC378.pin9, SN74HC379.pin8, SN74HC379.pin9, SN74HC381.pin8, SN74HC381.pin9
  N11: Part1.D9, Part5.D9, SW1.13, R34.Pin_0, LED56.anode, SN74HC377.pin12, SN74HC377.pin13, SN74HC379.pin12, SN74HC379.pin13
  N12: Part1.D10, Part5.D10, SW1.14, R35.Pin_0, LED57.anode, SN74HC377.pin14, SN74HC377.pin15, SN74HC379.pin14, SN74HC379.pin15
  N13: Part1.D11/MOSI, Part5.D11/MOSI, SW1.15, R33.Pin_0, LED59.anode, SN74HC377.pin16, SN74HC377.pin17, SN74HC379.pin16, SN74HC379.pin17
  N14: Part1.D12/MISO, Part5.D12/MISO, SW1.16, R32.Pin_0, LED58.anode, SN74HC377.pin18, SN74HC377.pin19, SN74HC379.pin18, SN74HC379.pin19
  VIN: Part1.VIN, Part5.VIN
  5V: Part1.5V, Part2.5V, Part5.5V, SW1.1, SW1.2, SW1.3, SW1.4, SW1.5, SW1.6, SW1.7, SW1.8, SN74HC377.pin20, SN74HC379.pin20, SN74HC374.pin20, SN74HC382.pin14, SN74HC383.pin14, SN74HC04.pin14, SN74HC32.pin14, SN74HC384.pin14, R43.Pin_1, R40.Pin_1, R41.Pin_1, R42.Pin_1
  N15: Part1.A7, Part5.A7
  N16: Part1.A6, Part5.A6
  N17: Part1.A5, Part2.A5, Part3.A5, Part4.A5, Part5.A5
  N18: Part1.A4, Part2.A4, Part3.A4, Part4.A4, Part5.A4
  N19: Part1.A3, Part5.A3, LED73.anode
  N20: Part1.A2, Part5.A2, U29.SH_CP
  N21: Part1.A1, Part5.A1, U29.ST_CP
  N22: Part1.A0, Part5.A0, U29.DS
  N23: Part1.AREF, Part5.AREF
  3V3: Part1.3V3, Part5.3V3
  N24: Part1.D13/SCK, Part5.D13/SCK
  N25: Part2.D2, LED80.anode
  N26: Part2.D5, LED79.anode
  N27: Part2.D6, LED78.anode
  N28: Part2.D7, LED77.anode
  N29: Part2.D8, SN74HC00.pin3
  N30: Part2.D9, SN74HC374.pin8
  N31: Part2.D10, SN74HC374.pin7
  N32: Part2.D11/MOSI, SN74HC374.pin4
  N33: Part2.D12/MISO, SN74HC374.pin3
  N34: Part2.A2, LED70.anode
  N35: Part2.A1, LED71.anode
  N36: Part2.A0, LED72.anode
  N37: Part3.D3, LED99.anode
  N38: Part3.D4, S1.Pin_3, S1.Pin_4
  N39: Part3.D5, LED91.anode
  N40: Part3.D6, LED90.anode
  N41: Part3.D7, LED89.anode
  N42: Part3.D8, LED86.anode
  N43: Part3.D9, LED88.anode
  N44: Part3.D10, LED87.anode
  N45: Part3.D11/MOSI, LED85.anode
  N46: Part3.D12/MISO, LED64.anode
  N47: Part4.D5, LED98.anode
  N48: Part4.D8, LED97.anode
  N49: Part4.D12/MISO, LED96.anode
  N50: LED41.cathode, R6.Pin_1
  N51: R7.Pin_1, LED53.cathode
  N52: R4.Pin_1, LED55.cathode
  N53: R3.Pin_1, LED56.cathode
  N54: R2.Pin_1, LED57.cathode
  N55: R8.Pin_1, LED59.cathode
  N56: R1.Pin_1, LED58.cathode
  N57: SN74HC373.pin1, SN74HC00.pin8
  N58: SN74HC376.pin1, SN74HC384.pin6
  N59: SN74HC376.pin10, SN74HC378.pin10, SN74HC379.pin10, SN74HC381.pin10, R44.Pin_0, R45.Pin_0, R47.Pin_0, R48.Pin_0, R49.Pin_0, R50.Pin_0, R51.Pin_0, R52.Pin_0, R53.Pin_0, R54.Pin_0
  N60: SN74HC377.pin1, SN74HC383.pin6
  N61: SN74HC377.pin11, LED102.anode
  N62: SN74HC379.pin1, SN74HC383.pin3
  N63: SN74HC374.pin2, LED68.anode, SN74HC380.pin1
  N64: SN74HC374.pin5, LED67.anode
  N65: LED65.cathode, R43.Pin_0
  N66: LED66.cathode, R40.Pin_0
  N67: LED67.cathode, R41.Pin_0
  N68: LED68.cathode, R42.Pin_0
  N69: LED83.anode, SN74HC32.pin5
  N70: LED84.anode, SN74HC00.pin5
  N71: SN74HC381.pin1, SN74HC384.pin3
  N72: LED85.cathode, R51.Pin_1
  N73: LED86.cathode, R47.Pin_1
  N74: LED87.cathode, R50.Pin_1
  N75: LED88.cathode, R48.Pin_1
  N76: LED89.cathode, R49.Pin_1
  N77: LED90.cathode, R45.Pin_1
  N78: LED91.cathode, R44.Pin_1
  N79: LED93.anode, SN74HC384.pin1, SN74HC384.pin2
  N80: LED99.cathode, R52.Pin_1
  N81: SN74HC382.pin8, SN74HC04.pin6, SN74HC32.pin4
  N82: SN74HC382.pin9, SN74HC382.pin10, SN74HC382.pin11
  N83: SN74HC382.pin12, LED105.anode
  N84: SN74HC382.pin13, SN74HC04.pin5, SN74HC32.pin3
  N85: LED101.anode, SN74HC384.pin4, SN74HC384.pin5
  N86: SN74HC383.pin1, SN74HC383.pin2, LED104.anode
  N87: SN74HC383.pin4, SN74HC383.pin5, LED103.anode
  N88: SN74HC04.pin7, SN74HC32.pin7
  N89: R54.Pin_1, LED64.cathode

notes:
  R0_e, R0_s, R1_e, R1_s
  IO_e, IO_s, IO_d, IO_a
  R2_e, R3_e, R2_s, R3_s, IAR_s
  FLAGS
  IAR
  R0
  R1
  R2
  R3
  HLT
  MAR_s
  RAM_s
  RAM_e
  Ctmp+enable, ~IAR_e
  IR
  ALU2
  ALU1
  ALU0
  Ctmp_e
  IAR_e
  IAR_s
  TMP_s
  ACC_s
  FLAGS_s
  BIT1
  ACC_e
  JCOND
  R0_e
  R1_e
  R0_s
  R1_s
  IR_s
  R2_e
  R3_e
  R3_s
  R2_s
